// Logisim project ICs.circ as structural Verilog: 10 circuits, main circuit IC 7408 (2-input AND)
module IC_7408__2_input_AND (
  input  in_1,
  input  in_2,
  input  in_3,
  input  in_4,
  input  in_5,
  input  in_6,
  input  in_7,
  input  in_8,
  output out_9,
  output out_10,
  output out_11,
  output out_12
);

  and and_1 (out_9, in_1, in_3);
  and and_2 (out_11, in_5, in_7);
  and and_3 (out_10, in_2, in_4);
  and and_4 (out_12, in_6, in_8);
endmodule

module IC_7411__3_input_AND (
  input  in_1,
  input  in_2,
  input  in_3,
  input  in_4,
  input  in_5,
  input  in_6,
  input  in_7,
  input  in_8,
  input  in_9,
  output out_10,
  output out_11,
  output out_12
);

  and and_1 (out_10, in_1, in_3, in_5);
  and and_2 (out_12, in_7, in_8, in_9);
  and and_3 (out_11, in_2, in_4, in_6);
endmodule

module IC_7432__2_input_OR (
  input  in_1,
  input  in_2,
  input  in_3,
  input  in_4,
  input  in_5,
  input  in_6,
  input  in_7,
  input  in_8,
  output out_9,
  output out_10,
  output out_11,
  output out_12
);

  or or_1 (out_9, in_1, in_3);
  or or_2 (out_11, in_5, in_7);
  or or_3 (out_10, in_2, in_4);
  or or_4 (out_12, in_6, in_8);
endmodule

module IC_4075__3_input_OR (
  input  in_1,
  input  in_2,
  input  in_3,
  input  in_4,
  input  in_5,
  input  in_6,
  input  in_7,
  input  in_8,
  input  in_9,
  output out_10,
  output out_11,
  output out_12
);

  or or_1 (out_10, in_1, in_3, in_5);
  or or_2 (out_12, in_7, in_8, in_9);
  or or_3 (out_11, in_2, in_4, in_6);
endmodule

module IC_7486__2_input_XOR (
  input  in_1,
  input  in_2,
  input  in_3,
  input  in_4,
  input  in_5,
  input  in_6,
  input  in_7,
  input  in_8,
  output out_9,
  output out_10,
  output out_11,
  output out_12
);

  xor xor_1 (out_9, in_1, in_3);
  xor xor_2 (out_11, in_5, in_7);
  xor xor_3 (out_10, in_2, in_4);
  xor xor_4 (out_12, in_6, in_8);
endmodule

module IC_4011__2_input_NAND (
  input  in_1,
  input  in_2,
  input  in_3,
  input  in_4,
  input  in_5,
  input  in_6,
  input  in_7,
  input  in_8,
  output out_9,
  output out_10,
  output out_11,
  output out_12
);

  nand nand_1 (out_9, in_1, in_3);
  nand nand_2 (out_11, in_5, in_7);
  nand nand_3 (out_10, in_2, in_4);
  nand nand_4 (out_12, in_6, in_8);
endmodule

module IC_7404__Inverters (
  input  in_1,
  input  in_2,
  input  in_3,
  input  in_4,
  input  in_5,
  input  in_6,
  output out_7,
  output out_8,
  output out_9,
  output out_10,
  output out_11,
  output out_12
);

  not not_1 (out_7, in_1);
  not not_2 (out_9, in_3);
  not not_3 (out_11, in_5);
  not not_4 (out_8, in_2);
  not not_5 (out_10, in_4);
  not not_6 (out_12, in_6);
endmodule

module IC_74153__2x_4_1_MUX (
  input  in_1,
  input  in_2,
  input  in_3,
  input  in_4,
  input  in_5,
  input  in_6,
  input  in_7,
  input  in_8,
  input  in_9,
  input  in_10,
  input  in_11,
  input  in_12,
  output out_13,
  output out_14
);

  wire and_1_out, and_2_out, and_3_out, and_4_out, and_5_out, and_6_out, and_7_out, and_8_out, not_1_out,
       not_2_out, not_3_out, not_4_out;

  not not_1 (not_1_out, in_1);
  not not_2 (not_2_out, in_2);
  not not_3 (not_3_out, in_3);
  not not_4 (not_4_out, in_8);
  and and_1 (and_1_out, in_4, not_3_out, not_2_out, not_1_out);
  and and_2 (and_2_out, in_5, not_3_out, in_2, not_1_out);
  and and_3 (and_3_out, in_6, in_3, not_2_out, not_1_out);
  and and_4 (and_4_out, in_7, in_3, in_2, not_1_out);
  and and_5 (and_5_out, in_9, not_3_out, not_2_out, not_4_out);
  and and_6 (and_6_out, in_10, not_3_out, in_2, not_4_out);
  and and_7 (and_7_out, in_11, in_3, not_2_out, not_4_out);
  and and_8 (and_8_out, in_12, in_3, in_2, not_4_out);
  or or_1 (out_13, and_1_out, and_2_out, and_3_out, and_4_out);
  or or_2 (out_14, and_5_out, and_6_out, and_7_out, and_8_out);
endmodule

module IC_7483__4_bit_Full_Adder (
  input  in_1,
  input  in_2,
  input  in_3,
  input  in_4,
  input  in_5,
  input  in_6,
  input  in_7,
  input  in_8,
  input  in_9,
  output out_10,
  output out_11,
  output out_12,
  output out_13,
  output out_14
);

  wire and_1_out, and_2_out, and_3_out, and_4_out, and_5_out, and_6_out, and_7_out, and_8_out, or_1_out,
       or_2_out, or_3_out, xor_1_out, xor_3_out, xor_5_out, xor_7_out;

  xor xor_1 (xor_1_out, in_1, in_5);
  and and_1 (and_1_out, xor_1_out, in_9);
  and and_2 (and_2_out, in_1, in_5);
  xor xor_2 (out_10, xor_1_out, in_9);
  or or_1 (or_1_out, and_1_out, and_2_out);
  xor xor_3 (xor_3_out, in_2, in_6);
  xor xor_4 (out_11, xor_3_out, or_1_out);
  and and_3 (and_3_out, xor_3_out, or_1_out);
  and and_4 (and_4_out, in_2, in_6);
  or or_2 (or_2_out, and_3_out, and_4_out);
  xor xor_5 (xor_5_out, in_3, in_7);
  xor xor_6 (out_12, xor_5_out, or_2_out);
  and and_5 (and_5_out, xor_5_out, or_2_out);
  and and_6 (and_6_out, in_3, in_7);
  or or_3 (or_3_out, and_5_out, and_6_out);
  xor xor_7 (xor_7_out, in_4, in_8);
  and and_7 (and_7_out, xor_7_out, or_3_out);
  and and_8 (and_8_out, in_4, in_8);
  xor xor_8 (out_13, xor_7_out, or_3_out);
  or or_4 (out_14, and_7_out, and_8_out);
endmodule

module _4_bit_Multiplier_IC__Customized (
  input  [3:0] A4_A3_A2_A1,
  input  [3:0] B4_B3_B2_B1,
  output S8,
  output S7,
  output S6,
  output S5,
  output S4,
  output S3,
  output S2,
  output S1
);

  wire ic_7408_2_input_and_1_out_10, ic_7408_2_input_and_1_out_11, ic_7408_2_input_and_1_out_12,
       ic_7408_2_input_and_2_out_9, ic_7408_2_input_and_2_out_10, ic_7408_2_input_and_2_out_11,
       ic_7408_2_input_and_2_out_12, ic_7408_2_input_and_3_out_9, ic_7408_2_input_and_3_out_10,
       ic_7408_2_input_and_3_out_11, ic_7408_2_input_and_3_out_12, ic_7408_2_input_and_4_out_9,
       ic_7408_2_input_and_4_out_10, ic_7408_2_input_and_4_out_11, ic_7408_2_input_and_4_out_12,
       ic_7483_4_bit_full_adder_1_out_11, ic_7483_4_bit_full_adder_1_out_12,
       ic_7483_4_bit_full_adder_1_out_13, ic_7483_4_bit_full_adder_1_out_14,
       ic_7483_4_bit_full_adder_2_out_11, ic_7483_4_bit_full_adder_2_out_12,
       ic_7483_4_bit_full_adder_2_out_13, ic_7483_4_bit_full_adder_2_out_14;

  IC_7408__2_input_AND ic_7408_2_input_and_1 (
    .in_1(A4_A3_A2_A1[0]), .in_3(B4_B3_B2_B1[0]), .out_9(S1), .in_5(A4_A3_A2_A1[0]), .in_7(B4_B3_B2_B1[1]),
    .out_11(ic_7408_2_input_and_1_out_11), .in_2(A4_A3_A2_A1[0]), .in_4(B4_B3_B2_B1[2]),
    .out_10(ic_7408_2_input_and_1_out_10), .in_6(A4_A3_A2_A1[0]), .in_8(B4_B3_B2_B1[3]),
    .out_12(ic_7408_2_input_and_1_out_12));
  IC_7408__2_input_AND ic_7408_2_input_and_2 (
    .in_1(A4_A3_A2_A1[1]), .in_3(B4_B3_B2_B1[0]), .out_9(ic_7408_2_input_and_2_out_9), .in_5(A4_A3_A2_A1[1]),
    .in_7(B4_B3_B2_B1[1]), .out_11(ic_7408_2_input_and_2_out_11), .in_2(A4_A3_A2_A1[1]),
    .in_4(B4_B3_B2_B1[2]), .out_10(ic_7408_2_input_and_2_out_10), .in_6(A4_A3_A2_A1[1]),
    .in_8(B4_B3_B2_B1[3]), .out_12(ic_7408_2_input_and_2_out_12));
  IC_7483__4_bit_Full_Adder ic_7483_4_bit_full_adder_1 (
    .in_1(ic_7408_2_input_and_1_out_11), .in_2(ic_7408_2_input_and_1_out_10),
    .in_3(ic_7408_2_input_and_1_out_12), .in_4(1'b0), .out_10(S2),
    .out_11(ic_7483_4_bit_full_adder_1_out_11), .out_12(ic_7483_4_bit_full_adder_1_out_12),
    .out_13(ic_7483_4_bit_full_adder_1_out_13), .in_5(ic_7408_2_input_and_2_out_9),
    .in_6(ic_7408_2_input_and_2_out_11), .in_7(ic_7408_2_input_and_2_out_10),
    .in_8(ic_7408_2_input_and_2_out_12), .in_9(1'b0), .out_14(ic_7483_4_bit_full_adder_1_out_14));
  IC_7408__2_input_AND ic_7408_2_input_and_3 (
    .in_1(A4_A3_A2_A1[2]), .in_3(B4_B3_B2_B1[0]), .out_9(ic_7408_2_input_and_3_out_9), .in_5(A4_A3_A2_A1[2]),
    .in_7(B4_B3_B2_B1[1]), .out_11(ic_7408_2_input_and_3_out_11), .in_2(A4_A3_A2_A1[2]),
    .in_4(B4_B3_B2_B1[2]), .out_10(ic_7408_2_input_and_3_out_10), .in_6(A4_A3_A2_A1[2]),
    .in_8(B4_B3_B2_B1[3]), .out_12(ic_7408_2_input_and_3_out_12));
  IC_7483__4_bit_Full_Adder ic_7483_4_bit_full_adder_2 (
    .in_1(ic_7483_4_bit_full_adder_1_out_11), .in_2(ic_7483_4_bit_full_adder_1_out_12),
    .in_3(ic_7483_4_bit_full_adder_1_out_13), .in_4(ic_7483_4_bit_full_adder_1_out_14), .out_10(S3),
    .out_11(ic_7483_4_bit_full_adder_2_out_11), .out_12(ic_7483_4_bit_full_adder_2_out_12),
    .out_13(ic_7483_4_bit_full_adder_2_out_13), .in_5(ic_7408_2_input_and_3_out_9),
    .in_6(ic_7408_2_input_and_3_out_11), .in_7(ic_7408_2_input_and_3_out_10),
    .in_8(ic_7408_2_input_and_3_out_12), .in_9(1'b0), .out_14(ic_7483_4_bit_full_adder_2_out_14));
  IC_7408__2_input_AND ic_7408_2_input_and_4 (
    .in_1(A4_A3_A2_A1[3]), .in_3(B4_B3_B2_B1[0]), .out_9(ic_7408_2_input_and_4_out_9), .in_5(A4_A3_A2_A1[3]),
    .in_7(B4_B3_B2_B1[1]), .out_11(ic_7408_2_input_and_4_out_11), .in_2(A4_A3_A2_A1[3]),
    .in_4(B4_B3_B2_B1[2]), .out_10(ic_7408_2_input_and_4_out_10), .in_6(A4_A3_A2_A1[3]),
    .in_8(B4_B3_B2_B1[3]), .out_12(ic_7408_2_input_and_4_out_12));
  IC_7483__4_bit_Full_Adder ic_7483_4_bit_full_adder_3 (
    .in_1(ic_7483_4_bit_full_adder_2_out_11), .in_2(ic_7483_4_bit_full_adder_2_out_12),
    .in_3(ic_7483_4_bit_full_adder_2_out_13), .in_4(ic_7483_4_bit_full_adder_2_out_14), .out_10(S4),
    .out_11(S5), .out_12(S6), .out_13(S7), .in_5(ic_7408_2_input_and_4_out_9),
    .in_6(ic_7408_2_input_and_4_out_11), .in_7(ic_7408_2_input_and_4_out_10),
    .in_8(ic_7408_2_input_and_4_out_12), .in_9(1'b0), .out_14(S8));
endmodule
